# Fritzing sketch TurretControlCircuitMAY22 (saved by Fritzing 0.9.3b)
breadboards: 3

parts:
  LED1 = LED - 5mm [color="Red (633nm)" package="5 mm [THT]"]
  U1 = ULN2003 [package=DIP-16]
  S1 = Momentary Switch [package=ksa_sealed_tac_switch]
  S2 = Momentary Switch [package=ksa_sealed_tac_switch]
  LCD1 = LCD screen
  R3 = 10k Resistor [package=THT]
  R4 = 10k Resistor [package=THT]
  IC1 = LM350T [package=to-220-alt]
  R5 = 150 ohm Resistor [package=THT]
  U4 = 12vd 1A PWR supply [package=lipo-110]
  JP2 = Header 5x2 [package=2x5-shrouded_smd]
  JP3 = Header 5x2 [package=2x5-shrouded_smd]
  JP4 = M16 [package=1x16_machine-pin-header_lock.004]
  U5 = LIPO-110mAh [package=lipo-110]
  D1 = Rectifier Diode [part_number=1N4004 package="300 mil [THT]"]
  R6 = 5K TRIMPOT [package=trimpot_pth_s3_lock]
  R7 = 10k TRIMPOT [package=trimpot_pth_s3_lock]
  R8 = 50k Rotary POT [package=THT]
  C4 = 10uf [package="100 mil [THT, electrolytic]"]
  C5 = Ceramic Cap [package="100 mil [THT, multilayer]"]
  C6 = Ceramic Capacitor [package="100 mil [THT, multilayer]"]
  C7 = Ceramic Capacitor [package="100 mil [THT, multilayer]"]

nets:
  N1: LED1.cathode, LCD1.VSS, LCD1.R/W, LCD1.LED-, R3.Pin_1, U5.-, R8.leg2, C6.1
  N2: LED1.anode, JP4.16
  N3: U1.IN_1, U1.IN_2, U1.IN_3, U1.IN_4, U1.IN_5, U1.IN_6, U1.OUT_6, U1.OUT_5, U1.OUT_4, U1.OUT_3, U1.OUT_2, U1.OUT_1, JP2.1, JP2.2, JP2.3, JP2.4, JP2.5, JP2.6, JP2.7, JP2.8, JP2.9, JP2.10, JP3.1, JP3.2, JP3.3, JP3.4, JP3.5, JP3.6, JP3.7, JP3.8, JP3.9, JP3.10
  N4: U1.IN_7, U1.OUT_7
  N5: U1.GND, U1.COM, IC1.OUT, IC1.IN, R5.Pin_1, U4.+, U4.-, D1.cathode, R6.CW, C4.-, C5.0, C5.1
  N6: S1.1, S1.2, R3.Pin_0
  N7: S1.3, S1.4, JP4.3, C7.0
  N8: S2.1, S2.2, R4.Pin_1
  N9: S2.3, S2.4, JP4.2, C6.0
  N10: LCD1.VDD, LCD1.LED+, U5.+, R7.CCW, R7.CW, R8.leg1
  N11: LCD1.V0, R7.WIPER
  N12: LCD1.RS, JP4.5
  N13: LCD1.E, JP4.6
  N14: LCD1.DB4, JP4.12
  N15: LCD1.DB5, JP4.13
  N16: LCD1.DB6, JP4.14
  N17: LCD1.DB7, JP4.15
  N18: R4.Pin_0, C7.1
  N19: IC1.GND_ADJ, R5.Pin_0, D1.anode, R6.CCW, R6.WIPER, C4.+
  N20: JP4.1, R8.wiper

notes:
  Driver is: SBT0811/ULN2003APG
  12vdc 1A
  5vdc 110mAh

custom parts:
  ULN2003: Current Driver IC
  10k Resistor: A generic resistor (0.25W)
  LM350T: Voltage Regulator Standard 7805 5V regulator. IGO (Input Ground Output). Spark Fun Electronics SKU : COM-00107
  150 ohm Resistor: A generic resistor (0.25W)
  12vd 1A PWR supply: 12vdc 1A PWR supply
  Rectifier Diode: A standard rectifier diode
  5K TRIMPOT: Various small potentiometers for set-and-forget applications
  10k TRIMPOT: Various small potentiometers for set-and-forget applications
  50k Rotary POT: A rotary adjustable resistor (potentiometer).
  10uf: A small electrolytic capacitor
  Ceramic Cap: 100 nF multilayer Ceramic Capacitor
  Ceramic Capacitor: 100 nF multilayer Ceramic Capacitor
