# Fritzing sketch TurretControlCircuitMay18 code (saved by Fritzing 0.9.3b)
breadboards: 2

parts:
  Part1 = Arduino Mega 2560 (Rev3)
  LED1 = LED - 5mm [color="Red (633nm)" package="5 mm [THT]"]
  R1 = Rotary Potentiometer (Small) [maximum_resistance=100kΩ package=THT]
  U1 = ULN2003 [package=DIP-16]
  M1 = Stepper Motor - Bipolar
  S1 = Momentary Switch [package=ksa_sealed_tac_switch]
  S2 = Momentary Switch [package=ksa_sealed_tac_switch]
  R2 = TRIMPOT [package=trimpot_pth_s3_lock]
  LCD1 = LCD screen
  R3 = 10k Resistor [package=THT]
  R4 = 10k Resistor [package=THT]
  C1 = Ceramic Capacitor [capacitance=100nF package="100 mil [THT, multilayer]"]
  C2 = Ceramic Capacitor [capacitance=100nF package="100 mil [THT, multilayer]"]
  IC1 = LM350T [package=to-220-alt]
  C3 = Ceramic Capacitor [capacitance=100nF package="100 mil [THT, multilayer]"]
  R5 = 150 ohm Resistor [package=THT]
  D1 = Rectifier Diode [part_number=1N4001 package="300 mil [THT]"]
  C5 = Electrolytic Capacitor [package="100 mil [THT, electrolytic]"]
  R6 = TRIMPOT [package=trimpot_pth_s3_lock]

nets:
  N1: Part1.A0, R1.wiper
  N2: Part1.D21/SCL, LCD1.RS
  N3: Part1.D19/RX1, LCD1.DB4
  N4: Part1.D18/TX1, LCD1.DB5
  N5: Part1.D17_PWM/RX2, LCD1.DB6
  N6: Part1.D16_PWM/TX2, LCD1.DB7
  N7: Part1.D13_PWM, LED1.anode
  N8: Part1.D12_PWM, U1.IN_1
  N9: Part1.D11_PWM, U1.IN_2
  N10: Part1.D10_PWM, U1.IN_3
  N11: Part1.D9_PWM, U1.IN_4
  5V: Part1.5V, R1.leg1, R2.CCW, LCD1.VDD, LCD1.LED+
  GND: Part1.GND, LED1.cathode, R1.leg2, R2.CW, LCD1.VSS, LCD1.R/W, LCD1.LED-, R3.Pin_1, R4.Pin_0, C1.1, C2.1
  N12: Part1.D2_PWM, S1.3, S1.4, C1.0
  N13: Part1.D3_PWM, S2.3, S2.4, C2.0
  N14: U1.GND, C3.1, C5.-, R6.CW
  N15: U1.COM, C3.0, R5.Pin_1, D1.cathode
  N16: U1.OUT_4, M1.A
  N17: U1.OUT_3, M1.C
  N18: U1.OUT_2, M1.B
  N19: U1.OUT_1, M1.D
  N20: S1.1, S1.2, R3.Pin_0
  N21: S2.1, S2.2, R4.Pin_1
  N22: R2.WIPER, LCD1.V0
  N23: IC1.GND_ADJ, R5.Pin_0, D1.anode, C5.+, R6.CCW, R6.WIPER

notes:
  *The stepper motor that is shown is NOT the motor that is on my protoboard
  StepperMTR is: 28BYJ-48
  Driver is: SBT0811/ULN2003APG
  Vol Reg LM350T with adjustable pin#1(GND)

custom parts:
  ULN2003: Current Driver IC
  10k Resistor: A generic resistor (0.25W)
  LM350T: Voltage Regulator Standard 7805 5V regulator. IGO (Input Ground Output). Spark Fun Electronics SKU : COM-00107
  150 ohm Resistor: A generic resistor (0.25W)
  Electrolytic Capacitor: A small electrolytic capacitor

// code stored in the sketch: turretontrol Code may18.ino
/*The circuit and code modified by me on 5/15/2017
  David H Haffner Sr as part of my prototype triple
  turret grating assembly, for my project 3D-Printable Raman Spectrometer
  http://hackaday.io/project/18126-3d-printable-raman-spectrometer
  The circuit as it stands now on a Mega 2560:
   LCD RS pin to digital pin 8
   LCD Enable pin to digital pin 9
   LCD D4 pin to digital pin 7
   LCD D5 pin to digital pin 6
   LCD D6 pin to digital pin 5
   LCD D7 pin to digital pin 4
   LCD R/W pin to ground
   LCD VSS pin to ground
   LCD VCC pin to 5V
   10K resistor:Trimmer POT
   ends to +5V and ground
   wiper to LCD VO pin (pin 3)

  Library originally added 18 Apr 2008
  by David A. Mellis
  library modified 5 Jul 2009
  by Limor Fried (http://www.ladyada.net)
  example added 9 Jul 2009
  by Tom Igoe
  modified 22 Nov 2010
  by Tom Igoe

  This example code is in the public domain.

  http://www.arduino.cc/en/Tutorial/LiquidCrystal
*/

// include the library code:

#include <LiquidCrystal.h>
#include <Stepper.h>
#include <LCDMenuLib.h>

const int button_1 = 1;// variable for storing button's status(this is for my referene :))
const int button_2 = 0;// variable for storing button's status
const int ledPin = 13;
const int motorPin1 = 12;// IN1 on motor control board
const int motorPin2 = 11;// IN2
const int motorPin3 = 10;// IN3
const int motorPin4 =  9; // IN4

//Variables will change
int ledState = HIGH;        //current state of the output pin
int buttonState;            //current reading from the input pin
int lastButtonState = LOW;  //the previous reading from the input pin

unsigned long lastDebounceTime = 0;
unsigned long debounceDelay = 50;

int val1 = 0;
int val2 = 0;

// initialize the library with the numbers of the interface pins
LiquidCrystal lcd(21, 20, 19, 18, 17, 16);

const int stepsPerRevolution = 200;
//   Here set the stepper motor rotation step how much is a circle

int dim = stepsPerRevolution;
//  Set the step motor number and pin

Stepper myStepper(stepsPerRevolution, 13, 12, 11, 10);

void setup() {

  pinMode(3, INPUT_PULLUP);//Sets the buttons as input
  pinMode(ledPin, OUTPUT);
  pinMode(2, INPUT_PULLUP);
  pinMode(ledPin, OUTPUT);
  //set initial LED state
  digitalWrite(ledPin, ledState);
  attachInterrupt(1, counterclockwise, FALLING);
  attachInterrupt(0, clockwise, FALLING);

  // set up the LCD's number of columns and rows:
  lcd.begin(16, 2);
  // Print a message to the LCD.
  lcd.print("Speed:");

  lcd.setCursor(10, 0);

  lcd.print("n/min");

  lcd.setCursor(0, 1);
  lcd.print("Direction:");

}

void loop() {
  //read the state of the switch into local variable
  int reading = digitalRead(button_1);
  int redaing = digitalRead(button_2);

  // check to see if U pressed the button
  //(i.e Input went from LOW to HIGH)

  // if switch changed, due to noise or pressing:
  if (reading != lastButtonState) {
    // reset the debouncing timer
    lastDebounceTime = millis();
  }

  if ((millis() - lastDebounceTime) > debounceDelay) {
    //whatever the reading is at, it's been there for longer
    // than the debounce delay, so take it as the actual current state:

    // if the button state has changed:
    if (reading != buttonState) {
      buttonState = reading;

      // only toggle the LED if the new button state is HIGH
      if (buttonState == HIGH) {
        ledState = !ledState;

      }
    }
  }
  myStepper.step(dim);
  void Direction();
  //  Read the sensor values:
  int sensorReading = analogRead(A0);
  //  Map it to a range of 0-150:
  int motorSpeed = map(sensorReading, 0, 1023, 0, 150);
  //  Set the motor speed:
  if (motorSpeed > 0)
    Serial.begin(115200);

  val1 = digitalRead(1);
  if (val1 == HIGH)

    val2 = digitalRead(0);
  if (val2 == HIGH)

  {

    myStepper.setSpeed(motorSpeed);
    lcd.setCursor(6, 0);
    lcd.print(float(float(motorSpeed) / float(200)));

  }

}

void clockwise()
{
  //   clockwise rotation
  dim = stepsPerRevolution;
  lcd.setCursor(10, 1);
  lcd.print(">>>>>>");

}


void counterclockwise()
{
  // anti-clockwise
  dim = -stepsPerRevolution;
  lcd.setCursor(10, 1);
  lcd.print("<<<<<<");
}
